// Logisim project Elevate-x.circ as structural Verilog: 7 circuits, main circuit main
module main (
  input  req_dirn,
  input  [2:0] req_floor,
  input  [2:0] l1_md,
  input  [2:0] l1,
  input  [2:0] l2_md,
  input  [2:0] l2,
  output [1:0] Assigneed_lift
);

  wire clk_out, Fullness_2_num, Fullness_num;
  wire [1:0] bit_extender_1_out, controller_1_assinged_lift;

  Clock clk (.out(clk_out));
  Fullness Fullness (.clk(clk_out), .num(Fullness_num));
  assign bit_extender_1_out = {{1{Fullness_num}}, Fullness_2_num};  // Bit_Extender bit_extender_1
  Fullness Fullness_2 (.clk(clk_out), .num(Fullness_2_num));
  controller controller_1 (
    .re_dirn(req_dirn), .req_floor(req_floor), .l1_md(l1_md), .L1_floor(l1), .l2_md(l2_md), .l2_floor(l2),
    .assinged_lift(controller_1_assinged_lift));
  Multiplexer #(.select(2), .width(2)) multiplexer_1 (
    .in0(controller_1_assinged_lift), .in1(2'b01), .in2(2'b10), .in3(2'b00), .out(Assigneed_lift),
    .sel(bit_extender_1_out), .en(1'b1));

  // Notes on the sheet:
  //   Controller
  //   How to use
  //   1. Give lift 1 current floor as l1 and lift 1 moving destination as l1_md  and similarly for lift 2
  //   2. Give requested floor and requested direction as req_floor and req_dirn respectively.
  //    3. Give a clock pulse clk and we will get our assinged lift as output Assigned_lift.
  //   4. 00 for no lift available ,01 for 1st lift assigned and 10 for second lift assigned.
endmodule

module difference (
  input  [2:0] l1,
  input  [2:0] l2,
  input  [2:0] req_flr,
  input  clk,
  output [1:0] assigned_lift
);

  wire comparator_1_eq, comparator_1_gt, comparator_1_lt, comparator_2_eq, comparator_2_gt, comparator_2_lt,
       comparator_3_gt, or_1_out, or_2_out;
  wire [2:0] multiplexer_1_out, multiplexer_2_out, register_1_q, register_2_q, register_3_q, register_4_q,
       subtractor_1_out, subtractor_2_out, subtractor_3_out, subtractor_4_out;

  Comparator #(.width(3), .mode("unsigned")) comparator_1 (
    .a(req_flr), .b(l1), .gt(comparator_1_gt), .eq(comparator_1_eq), .lt(comparator_1_lt));
  Comparator #(.width(3), .mode("unsigned")) comparator_2 (
    .a(req_flr), .b(l2), .gt(comparator_2_gt), .eq(comparator_2_eq), .lt(comparator_2_lt));
  or or_1 (or_1_out, comparator_1_gt, comparator_1_eq);
  or or_2 (or_2_out, comparator_2_gt, comparator_2_eq);
  Register #(.width(3)) register_1 (.D(req_flr), .en(comparator_1_lt), .Q(register_1_q), .clk(clk));  // open: clr
  Register #(.width(3)) register_2 (.D(req_flr), .en(comparator_2_lt), .Q(register_2_q), .clk(clk));  // open: clr
  Register #(.width(3)) register_3 (.D(req_flr), .en(or_1_out), .Q(register_3_q), .clk(clk));  // open: clr
  Subtractor #(.width(3)) subtractor_1 (.a(l1), .b(register_1_q), .out(subtractor_1_out));  // open: bin, bout
  Register #(.width(3)) register_4 (.D(req_flr), .en(or_2_out), .Q(register_4_q), .clk(clk));  // open: clr
  Subtractor #(.width(3)) subtractor_2 (.a(l2), .b(register_2_q), .out(subtractor_2_out));  // open: bin, bout
  Subtractor #(.width(3)) subtractor_3 (.a(register_3_q), .b(l1), .out(subtractor_3_out));  // open: bin, bout
  Subtractor #(.width(3)) subtractor_4 (.a(register_4_q), .b(l2), .out(subtractor_4_out));  // open: bin, bout
  Multiplexer #(.width(3)) multiplexer_1 (
    .in0(subtractor_3_out), .in1(subtractor_1_out), .out(multiplexer_1_out), .sel(comparator_1_lt), .en(1'b1));
  Multiplexer #(.width(3)) multiplexer_2 (
    .in0(subtractor_4_out), .in1(subtractor_2_out), .out(multiplexer_2_out), .sel(comparator_2_lt), .en(1'b1));
  Comparator #(.width(3), .mode("unsigned")) comparator_3 (
    .a(multiplexer_1_out), .b(multiplexer_2_out), .gt(comparator_3_gt));  // open: eq, lt
  Multiplexer #(.width(2)) multiplexer_3 (
    .in0(2'b01), .in1(2'b10), .out(assigned_lift), .sel(comparator_3_gt), .en(1'b1));
endmodule

module Fullness (
  input  clk,
  output num
);

  wire [3:0] Random_Generator_out;

  Random #(.width(4)) Random_Generator (.clk(clk), .next(1'b1), .out(Random_Generator_out), .clr(1'b0));
  Comparator #(.width(4), .mode("unsigned")) comparator_1 (
    .a(Random_Generator_out), .b(4'b1100), .gt(num));  // open: eq, lt

  // Notes on the sheet:
  //   Comparator
endmodule

module diff (
  input  [2:0] l1,
  input  [2:0] l2,
  input  [2:0] req_flr,
  output [1:0] assigned_lift
);

  wire comparator_1_gt, subtractor_1_bout, subtractor_3_bout;
  wire [2:0] multiplexer_1_out, multiplexer_2_out, subtractor_1_out, subtractor_2_out, subtractor_3_out,
       subtractor_4_out;

  Subtractor #(.width(3)) subtractor_1 (
    .a(l1), .b(req_flr), .out(subtractor_1_out), .bout(subtractor_1_bout));  // open: bin
  Subtractor #(.width(3)) subtractor_2 (.a(req_flr), .b(l1), .out(subtractor_2_out));  // open: bin, bout
  Subtractor #(.width(3)) subtractor_3 (
    .a(l2), .b(req_flr), .out(subtractor_3_out), .bout(subtractor_3_bout));  // open: bin
  Subtractor #(.width(3)) subtractor_4 (.a(req_flr), .b(l2), .out(subtractor_4_out));  // open: bin, bout
  Multiplexer #(.width(3), .enable("false")) multiplexer_1 (
    .in0(subtractor_1_out), .in1(subtractor_2_out), .out(multiplexer_1_out), .sel(subtractor_1_bout));
  Multiplexer #(.width(3), .enable("false")) multiplexer_2 (
    .in0(subtractor_3_out), .in1(subtractor_4_out), .out(multiplexer_2_out), .sel(subtractor_3_bout));
  Comparator #(.width(3), .mode("unsigned")) comparator_1 (
    .a(multiplexer_1_out), .b(multiplexer_2_out), .gt(comparator_1_gt));  // open: eq, lt
  Multiplexer #(.width(2)) multiplexer_3 (
    .in0(2'b01), .in1(2'b10), .out(assigned_lift), .sel(comparator_1_gt), .en(1'b1));
endmodule

module controller (
  input  re_dirn,
  input  [2:0] req_floor,
  input  [2:0] l1_md,
  input  [2:0] L1_floor,
  input  [2:0] l2_md,
  input  [2:0] l2_floor,
  output [1:0] assinged_lift
);

  wire comparator_1_lt, comparator_2_lt, comparator_3_lt, comparator_4_lt;
  wire [1:0] bit_extender_1_out, diff_1_assigned_lift, diff_2_assigned_lift;
  wire [2:0] bit_extender_2_out;
  wire [3:0] bit_extender_3_out;
  wire [4:0] bit_extender_4_out;

  Comparator #(.width(3), .mode("unsigned")) comparator_1 (
    .a(req_floor), .b(L1_floor), .lt(comparator_1_lt));  // open: gt, eq
  Comparator #(.width(3), .mode("unsigned")) comparator_2 (
    .a(req_floor), .b(l2_floor), .lt(comparator_2_lt));  // open: gt, eq
  Comparator #(.width(3), .mode("unsigned")) comparator_3 (
    .a(l1_md), .b(L1_floor), .lt(comparator_3_lt));  // open: gt, eq
  Comparator #(.width(3), .mode("unsigned")) comparator_4 (
    .a(l2_md), .b(l2_floor), .lt(comparator_4_lt));  // open: gt, eq
  diff diff_1 (.l1(L1_floor), .l2(l2_floor), .req_flr(req_floor), .assigned_lift(diff_1_assigned_lift));
  diff diff_2 (.l1(l1_md), .l2(l2_md), .req_flr(req_floor), .assigned_lift(diff_2_assigned_lift));
  assign bit_extender_1_out = {{1{comparator_4_lt}}, comparator_2_lt};  // Bit_Extender bit_extender_1
  assign bit_extender_2_out = {{1{comparator_1_lt}}, bit_extender_1_out};  // Bit_Extender bit_extender_2
  assign bit_extender_3_out = {{1{comparator_3_lt}}, bit_extender_2_out};  // Bit_Extender bit_extender_3
  assign bit_extender_4_out = {{1{re_dirn}}, bit_extender_3_out};  // Bit_Extender bit_extender_4
  Multiplexer #(.select(5), .width(2)) multiplexer_1 (
    .in0(diff_2_assigned_lift), .in1(diff_2_assigned_lift), .in2(2'b01), .in3(2'b10),
    .in4(diff_2_assigned_lift), .in5(diff_2_assigned_lift), .in6(diff_2_assigned_lift), .in7(2'b10),
    .in8(2'b10), .in9(diff_2_assigned_lift), .in10(diff_2_assigned_lift), .in11(2'b10), .in12(2'b01),
    .in13(2'b01), .in14(2'b01), .in15(diff_1_assigned_lift), .in16(diff_1_assigned_lift), .in17(2'b01),
    .in18(2'b01), .in19(2'b01), .in20(2'b10), .in21(diff_2_assigned_lift), .in22(diff_2_assigned_lift),
    .in23(2'b10), .in24(2'b10), .in25(2'b10), .in26(diff_2_assigned_lift), .in27(diff_2_assigned_lift),
    .in28(2'b10), .in29(diff_2_assigned_lift), .in30(diff_2_assigned_lift), .in31(diff_2_assigned_lift),
    .out(assinged_lift), .sel(bit_extender_4_out), .en(1'b1));
endmodule

module Comparater (
  input  a1,
  input  a0,
  input  b1,
  input  b0,
  output X,
  output Y,
  output Z
);

  wire and_1_out, and_2_out, and_4_out, and_5_out, not_1_out, not_2_out, not_3_out, not_4_out, xnor_1_out,
       xnor_2_out, xnor_3_out, xnor_4_out;

  not not_1 (not_1_out, b1);
  xnor xnor_1 (xnor_1_out, a1, b1);
  not not_2 (not_2_out, b0);
  xnor xnor_2 (xnor_2_out, a1, b1);
  xnor xnor_3 (xnor_3_out, a0, b0);
  not not_3 (not_3_out, a1);
  xnor xnor_4 (xnor_4_out, a1, b1);
  not not_4 (not_4_out, a0);
  and and_1 (and_1_out, a1, not_1_out);
  and and_2 (and_2_out, xnor_1_out, a0, not_2_out);
  and and_3 (Y, xnor_2_out, xnor_3_out);
  and and_4 (and_4_out, not_3_out, b1);
  and and_5 (and_5_out, xnor_4_out, not_4_out, b0);
  or or_1 (X, and_1_out, and_2_out);
  or or_2 (Z, and_4_out, and_5_out);
endmodule

module subtracter (
  input  a1,
  input  a0,
  input  b1,
  input  b0,
  output s1,
  output s0,
  output Cout
);

  wire and_1_out, and_2_out, and_3_out, not_1_out, not_2_out, not_3_out, xnor_1_out, xor_2_out;

  not not_1 (not_1_out, a0);
  and and_1 (and_1_out, not_1_out, b0);
  xor xor_1 (s0, a0, b0);
  not not_2 (not_2_out, a1);
  not not_3 (not_3_out, a0);
  xnor xnor_1 (xnor_1_out, a1, b1);
  xor xor_2 (xor_2_out, a1, b1);
  and and_2 (and_2_out, not_2_out, b1);
  and and_3 (and_3_out, not_3_out, b0, xnor_1_out);
  xor xor_3 (s1, xor_2_out, and_1_out);
  or or_1 (Cout, and_2_out, and_3_out);
endmodule
